// Logisim project AMB.circ as structural Verilog: 1 circuit, main circuit AMB
module AMB (
  input  [11:0] \KY1_Veri_Giriş ,
  input  [1:0] \AMB_Denetim_Giriş ,
  input  [11:0] \KY2_Veri_Giriş ,
  output [11:0] \AMB_Sonuç_Çıkış ,
  output \ESD_Çıkış 
);

  wire [11:0] adder_1_out, nand_1_out, subtractor_1_out;

  Adder #(.width(12)) adder_1 (.a(\KY1_Veri_Giriş ), .b(\KY2_Veri_Giriş ), .out(adder_1_out));  // open: cin, cout
  Subtractor #(.width(12)) subtractor_1 (
    .a(\KY1_Veri_Giriş ), .b(\KY2_Veri_Giriş ), .out(subtractor_1_out));  // open: bin, bout
  assign nand_1_out = ~(\KY1_Veri_Giriş  & \KY2_Veri_Giriş );  // NAND_Gate nand_1, 12 bits wide
  Comparator #(.width(12)) comparator_1 (.a(\KY1_Veri_Giriş ), .b(\KY2_Veri_Giriş ), .eq(\ESD_Çıkış ));  // open: gt, lt
  Multiplexer #(.select(2), .width(12)) multiplexer_1 (
    .in0(adder_1_out), .in1(subtractor_1_out), .in2(nand_1_out), .in3({12{1'b1}}), .out(\AMB_Sonuç_Çıkış ),
    .sel(\AMB_Denetim_Giriş ));  // open: en
endmodule
