// Logisim project Anlik Toplayici.circ as structural Verilog: 1 circuit, main circuit Anlık Toplayıcı
module \Anlık_Toplayıcı  (
  input  [2:0] \Anlık_Girişi ,
  input  [11:0] \KY_Veri_Girişi ,
  output [14:0] \Toplam_Çıkış 
);

  wire [14:0] bit_extender_1_out;

  assign bit_extender_1_out = {{3{1'b0}}, \KY_Veri_Girişi };  // Bit_Extender bit_extender_1
  Adder #(.width(15)) adder_1 (
    .a({\Anlık_Girişi , {12{1'b0}}}), .b(bit_extender_1_out), .out(\Toplam_Çıkış ));  // open: cin, cout
endmodule
