// Logisim project Buyruk Bellegi.circ as structural Verilog: 1 circuit, main circuit Buyruk Belleği
module \Buyruk_Belleği  (
  input  [23:0] \Adres_Giriş ,
  output [11:0] \Buyruk_Çıkışı 
);

  ROM #(.addrWidth(24), .dataWidth(12)) rom_1 (.addr(\Adres_Giriş ), .data(\Buyruk_Çıkışı ));  // open: sel
endmodule
