// Logisim project Denetim.circ as structural Verilog: 1 circuit, main circuit Denetim
module Denetim (
  input  [11:0] \Buyruk_Girişi ,
  output [2:0] \HY_Anlık_Çıkış ,
  output [2:0] \KY2_Anlık_Çıkış ,
  output [2:0] \KY1_Çıkış ,
  output \Veri_Belleği_Adres_Denetim_Çıkış ,
  output [1:0] \AMB_Denetim_Çıkış ,
  output \HY_Veri_Denetim_Çıkış ,
  output \Yazmaç_Öbeği_Yazma_Denetimi_Çıkış ,
  output \Yüklesin_Mi_Denetim_Çıkış ,
  output \Saklasın_Mı_Denetim_Çıkış ,
  output \Dallanma_Denetim_Çıkış 
);

  and and_1 (\HY_Veri_Denetim_Çıkış , \Buyruk_Girişi [9], \Buyruk_Girişi [10]);
  not not_1 (\Yazmaç_Öbeği_Yazma_Denetimi_Çıkış , \Buyruk_Girişi [11]);
  Comparator #(.width(3)) comparator_1 (
    .a(\Buyruk_Girişi [11:9]), .b(3'b011), .eq(\Yüklesin_Mi_Denetim_Çıkış ));  // open: gt, lt
  Comparator #(.width(3)) comparator_2 (
    .a(\Buyruk_Girişi [11:9]), .b(3'b100), .eq(\Saklasın_Mı_Denetim_Çıkış ));  // open: gt, lt
  Comparator #(.width(3)) comparator_3 (
    .a(\Buyruk_Girişi [11:9]), .b(3'b101), .eq(\Dallanma_Denetim_Çıkış ));  // open: gt, lt

  assign \AMB_Denetim_Çıkış  = \Buyruk_Girişi [10:9];
  assign \HY_Anlık_Çıkış  = \Buyruk_Girişi [2:0];
  assign \KY1_Çıkış  = \Buyruk_Girişi [8:6];
  assign \KY2_Anlık_Çıkış  = \Buyruk_Girişi [5:3];
  assign \Veri_Belleği_Adres_Denetim_Çıkış  = \Buyruk_Girişi [11];
endmodule
