// Logisim project Hedef Yazmaci Secim.circ as structural Verilog: 1 circuit, main circuit Hedef Yazmacı Seçim
module \Hedef_Yazmacı_Seçim  (
  input  \HY_Secim_Giriş ,
  input  [11:0] AMB_Secimi,
  input  [11:0] \Veri_Belleği_Seçimi ,
  output [11:0] \HY_Seçim_Çıkış 
);

  Multiplexer #(.width(12)) multiplexer_1 (
    .in0(AMB_Secimi), .in1(\Veri_Belleği_Seçimi ), .out(\HY_Seçim_Çıkış ), .sel(\HY_Secim_Giriş ));  // open: en

  // Notes on the sheet:
  //   HY Seçim Girişi: 0 ise AMB, 1 ise Veri Belleği Seçilir
endmodule
