// Logisim project Islemci.circ as structural Verilog: 1 circuit, main circuit İşlemci
module \İşlemci  (
);

  wire \amb_1_esd_çıkış , clock_1_out, \denetim_1_dallanma_denetim_çıkış , \denetim_1_hy_veri_denetim_çıkış ,
       \denetim_1_saklasın_mı_denetim_çıkış , \denetim_1_veri_belleği_adres_denetim_çıkış ,
       \denetim_1_yazmaç_öbeği_yazma_denetimi_çıkış , \denetim_1_yüklesin_mi_denetim_çıkış ,
       \program_sayacı_1_saat_çıkışı ;
  wire [1:0] \denetim_1_amb_denetim_çıkış ;
  wire [2:0] \denetim_1_hy_anlık_çıkış , \denetim_1_ky1_çıkış , \denetim_1_ky2_anlık_çıkış ;
  wire [11:0] \amb_1_amb_sonuç_çıkış , \buyruk_belleği_1_buyruk_çıkışı ,
       \hedef_yazmacı_seçim_1_hy_seçim_çıkış , \veri_belleği_1_veri_çıkışı , \yazmaç_öbeği_1_ky1_veri_çıkış ,
       \yazmaç_öbeği_1_ky2_veri_çıkış ;
  wire [14:0] \anlık_toplayıcı_1_toplam_çıkış , \anlık_toplayıcı_2_toplam_çıkış ,
       \veri_belleği_adres_seçim_1_veri_belleği_adres_seçimi_çıkış ;
  wire [23:0] \program_sayacı_1_program_sayacı_çıkışı ;

  Clock clock_1 (.out(clock_1_out));
  \Program_Sayacı  \program_sayacı_1  (
    .\Dallanma_Mı_Girşi (\amb_1_esd_çıkış ), .\Dallanma_Anlık_Girişi (\denetim_1_hy_anlık_çıkış ),
    .\Saat_Girişi (clock_1_out), .\Program_Sayacı_Çıkışı (\program_sayacı_1_program_sayacı_çıkışı ),
    .\Saat_Çıkışı (\program_sayacı_1_saat_çıkışı ),
    .\Dallanma_Denetim_Giriş (\denetim_1_dallanma_denetim_çıkış ));
  \Veri_Belleği  \veri_belleği_1  (
    .\Adres_Girişi (\veri_belleği_adres_seçim_1_veri_belleği_adres_seçimi_çıkış ),
    .\Veri_Girişi (\yazmaç_öbeği_1_ky1_veri_çıkış ), .\Saklasın_Mı (\denetim_1_saklasın_mı_denetim_çıkış ),
    .\Saat_Girişi (\program_sayacı_1_saat_çıkışı ), .\Yüklesin_Mi (\denetim_1_yüklesin_mi_denetim_çıkış ),
    .\Veri_Çıkışı (\veri_belleği_1_veri_çıkışı ));  // open: Sıfırlasın_Mı
  \Veri_Belleği_Adres_Seçim  \veri_belleği_adres_seçim_1  (
    .\Veri_Belleği_Adres_Seçimi_Giriş (\denetim_1_veri_belleği_adres_denetim_çıkış ),
    .\Yükle_Anlık_Seçimi (\anlık_toplayıcı_1_toplam_çıkış ),
    .\Sakla_Anlık_Seçimi (\anlık_toplayıcı_2_toplam_çıkış ),
    .\Veri_Belleği_Adres_Seçimi_Çıkış (\veri_belleği_adres_seçim_1_veri_belleği_adres_seçimi_çıkış ));
  \Buyruk_Belleği  \buyruk_belleği_1  (
    .\Adres_Giriş (\program_sayacı_1_program_sayacı_çıkışı ),
    .\Buyruk_Çıkışı (\buyruk_belleği_1_buyruk_çıkışı ));
  \Anlık_Toplayıcı  \anlık_toplayıcı_1  (
    .\Anlık_Girişi (\denetim_1_ky2_anlık_çıkış ), .\KY_Veri_Girişi (\yazmaç_öbeği_1_ky1_veri_çıkış ),
    .\Toplam_Çıkış (\anlık_toplayıcı_1_toplam_çıkış ));
  \Anlık_Toplayıcı  \anlık_toplayıcı_2  (
    .\Anlık_Girişi (\denetim_1_hy_anlık_çıkış ), .\KY_Veri_Girişi (\yazmaç_öbeği_1_ky2_veri_çıkış ),
    .\Toplam_Çıkış (\anlık_toplayıcı_2_toplam_çıkış ));
  AMB amb_1 (
    .\KY1_Veri_Giriş (\yazmaç_öbeği_1_ky1_veri_çıkış ), .\AMB_Denetim_Giriş (\denetim_1_amb_denetim_çıkış ),
    .\KY2_Veri_Giriş (\yazmaç_öbeği_1_ky2_veri_çıkış ), .\AMB_Sonuç_Çıkış (\amb_1_amb_sonuç_çıkış ),
    .\ESD_Çıkış (\amb_1_esd_çıkış ));
  Denetim denetim_1 (
    .\Buyruk_Girişi (\buyruk_belleği_1_buyruk_çıkışı ), .\KY2_Anlık_Çıkış (\denetim_1_ky2_anlık_çıkış ),
    .\KY1_Çıkış (\denetim_1_ky1_çıkış ), .\HY_Anlık_Çıkış (\denetim_1_hy_anlık_çıkış ),
    .\Yazmaç_Öbeği_Yazma_Denetimi_Çıkış (\denetim_1_yazmaç_öbeği_yazma_denetimi_çıkış ),
    .\HY_Veri_Denetim_Çıkış (\denetim_1_hy_veri_denetim_çıkış ),
    .\AMB_Denetim_Çıkış (\denetim_1_amb_denetim_çıkış ),
    .\Yüklesin_Mi_Denetim_Çıkış (\denetim_1_yüklesin_mi_denetim_çıkış ),
    .\Saklasın_Mı_Denetim_Çıkış (\denetim_1_saklasın_mı_denetim_çıkış ),
    .\Veri_Belleği_Adres_Denetim_Çıkış (\denetim_1_veri_belleği_adres_denetim_çıkış ),
    .\Dallanma_Denetim_Çıkış (\denetim_1_dallanma_denetim_çıkış ));
  \Yazmaç_Öbeği  \yazmaç_öbeği_1  (
    .\Saat_Girişi (\program_sayacı_1_saat_çıkışı ), .\HY_Adres_Giriş (\denetim_1_hy_anlık_çıkış ),
    .\HY_Veri_Giriş (\hedef_yazmacı_seçim_1_hy_seçim_çıkış ),
    .\KY1_Veri_Çıkış (\yazmaç_öbeği_1_ky1_veri_çıkış ), .\KY1_Adres_Giriş (\denetim_1_ky1_çıkış ),
    .\KY2_Veri_Çıkış (\yazmaç_öbeği_1_ky2_veri_çıkış ), .\KY2_Adres_Giriş (\denetim_1_ky2_anlık_çıkış ),
    .\Yazma_Denetimi_Giriş (\denetim_1_yazmaç_öbeği_yazma_denetimi_çıkış ));
  \Hedef_Yazmacı_Seçim  \hedef_yazmacı_seçim_1  (
    .\HY_Secim_Giriş (\denetim_1_hy_veri_denetim_çıkış ), .AMB_Secimi(\amb_1_amb_sonuç_çıkış ),
    .\Veri_Belleği_Seçimi (\veri_belleği_1_veri_çıkışı ),
    .\HY_Seçim_Çıkış (\hedef_yazmacı_seçim_1_hy_seçim_çıkış ));
endmodule
