// Logisim project Program Sayaci.circ as structural Verilog: 1 circuit, main circuit Program Sayacı
module \Program_Sayacı  (
  input  \Dallanma_Denetim_Giriş ,
  input  \Dallanma_Mı_Girşi ,
  input  [2:0] \Dallanma_Anlık_Girişi ,
  input  \Saat_Girişi ,
  output [23:0] \Program_Sayacı_Çıkışı ,
  output \Saat_Çıkışı 
);

  wire and_1_out, and_2_out, comparator_1_eq, comparator_1_gt, or_1_out;
  wire [23:0] adder_1_out, bit_extender_1_out, buffer_1_out, multiplexer_1_out, multiplexer_2_out,
       subtractor_1_out;

  and and_1 (and_1_out, \Dallanma_Denetim_Giriş , \Dallanma_Mı_Girşi );
  assign bit_extender_1_out = {{19{1'b0}}, {\Dallanma_Anlık_Girişi [1:0], 3'b000}};  // Bit_Extender bit_extender_1
  Multiplexer #(.width(24)) multiplexer_1 (
    .in0(24'h1), .in1(bit_extender_1_out), .out(multiplexer_1_out), .sel(and_1_out));  // open: en
  Comparator #(.width(24)) comparator_1 (
    .a({24{1'b1}}), .b(\Program_Sayacı_Çıkışı ), .gt(comparator_1_gt), .eq(comparator_1_eq));  // open: lt
  assign buffer_1_out = multiplexer_2_out;  // Buffer buffer_1, 24 bits wide
  and and_2 (and_2_out, and_1_out, \Dallanma_Anlık_Girişi [2]);
  Register #(.width(24)) register_1 (
    .D(buffer_1_out), .Q(\Program_Sayacı_Çıkışı ), .clk(\Saat_Girişi ), .clr(or_1_out));  // open: en
  or or_1 (or_1_out, comparator_1_gt, comparator_1_eq);
  Multiplexer #(.width(24)) multiplexer_2 (
    .in0(adder_1_out), .in1(subtractor_1_out), .out(multiplexer_2_out), .sel(and_2_out));  // open: en
  Adder #(.width(24)) adder_1 (
    .a(multiplexer_1_out), .b(\Program_Sayacı_Çıkışı ), .out(adder_1_out));  // open: cin, cout
  Subtractor #(.width(24)) subtractor_1 (
    .a(\Program_Sayacı_Çıkışı ), .b(multiplexer_1_out), .out(subtractor_1_out));  // open: bin, bout

  assign \Saat_Çıkışı  = \Saat_Girişi ;
endmodule
