// Logisim project Veri Bellegi Adres Secim.circ as structural Verilog: 1 circuit, main circuit Veri Belleği Adres Seçim
module \Veri_Belleği_Adres_Seçim  (
  input  \Veri_Belleği_Adres_Seçimi_Giriş ,
  input  [14:0] \Yükle_Anlık_Seçimi ,
  input  [14:0] \Sakla_Anlık_Seçimi ,
  output [14:0] \Veri_Belleği_Adres_Seçimi_Çıkış 
);

  Multiplexer #(.width(15)) multiplexer_1 (
    .in0(\Yükle_Anlık_Seçimi ), .in1(\Sakla_Anlık_Seçimi ), .out(\Veri_Belleği_Adres_Seçimi_Çıkış ),
    .sel(\Veri_Belleği_Adres_Seçimi_Giriş ));  // open: en

  // Notes on the sheet:
  //   Veri Belleği Adres Seçim Girişi: 0 ise Yükle, 1 ise Sakla Seçilir
endmodule
