// Logisim project Veri Bellegi.circ as structural Verilog: 1 circuit, main circuit Veri Belleği
module \Veri_Belleği  (
  input  [14:0] \Adres_Girişi ,
  input  [11:0] \Veri_Girişi ,
  input  \Saklasın_Mı ,
  input  \Saat_Girişi ,
  input  \Yüklesin_Mi ,
  input  \Sıfırlasın_Mı ,
  output [11:0] \Veri_Çıkışı 
);

  RAM #(.addrWidth(15), .dataWidth(12), .bus("separate")) ram_1 (
    .addr(\Adres_Girişi ), .din(\Veri_Girişi ), .data(\Veri_Çıkışı ), .str(\Saklasın_Mı ),
    .clk(\Saat_Girişi ), .ld(\Yüklesin_Mi ), .clr(\Sıfırlasın_Mı ));  // open: sel
endmodule
