// Logisim project Yazmac Obegi.circ as structural Verilog: 1 circuit, main circuit Yazmaç Öbeği
module \Yazmaç_Öbeği  (
  input  \Yazma_Denetimi_Giriş ,
  input  \Saat_Girişi ,
  input  [2:0] \HY_Adres_Giriş ,
  input  [11:0] \HY_Veri_Giriş ,
  input  [2:0] \KY1_Adres_Giriş ,
  input  [2:0] \KY2_Adres_Giriş ,
  output [11:0] \KY1_Veri_Çıkış ,
  output [11:0] \KY2_Veri_Çıkış 
);

  wire demultiplexer_1_out0, demultiplexer_1_out1, demultiplexer_1_out2, demultiplexer_1_out3,
       demultiplexer_1_out4, demultiplexer_1_out5, demultiplexer_1_out6, demultiplexer_1_out7;
  wire [11:0] demultiplexer_2_out0, demultiplexer_2_out1, demultiplexer_2_out2, demultiplexer_2_out3,
       demultiplexer_2_out4, demultiplexer_2_out5, demultiplexer_2_out6, demultiplexer_2_out7, register_1_q,
       register_2_q, register_3_q, register_4_q, register_5_q, register_6_q, register_7_q, register_8_q;

  Demultiplexer #(.select(3)) demultiplexer_1 (
    .out0(demultiplexer_1_out0), .out1(demultiplexer_1_out1), .out2(demultiplexer_1_out2),
    .out3(demultiplexer_1_out3), .out4(demultiplexer_1_out4), .out5(demultiplexer_1_out5),
    .out6(demultiplexer_1_out6), .out7(demultiplexer_1_out7), .in(\Yazma_Denetimi_Giriş ),
    .sel(\HY_Adres_Giriş ));  // open: en
  Demultiplexer #(.select(3), .width(12)) demultiplexer_2 (
    .out0(demultiplexer_2_out0), .out1(demultiplexer_2_out1), .out2(demultiplexer_2_out2),
    .out3(demultiplexer_2_out3), .out4(demultiplexer_2_out4), .out5(demultiplexer_2_out5),
    .out6(demultiplexer_2_out6), .out7(demultiplexer_2_out7), .in(\HY_Veri_Giriş ), .sel(\HY_Adres_Giriş ));  // open: en
  Register #(.width(12)) register_1 (
    .D(demultiplexer_2_out0), .en(demultiplexer_1_out0), .Q(register_1_q), .clk(\Saat_Girişi ));  // open: clr
  Register #(.width(12)) register_2 (
    .D(demultiplexer_2_out1), .en(demultiplexer_1_out1), .Q(register_2_q), .clk(\Saat_Girişi ));  // open: clr
  Register #(.width(12)) register_3 (
    .D(demultiplexer_2_out2), .en(demultiplexer_1_out2), .Q(register_3_q), .clk(\Saat_Girişi ));  // open: clr
  Register #(.width(12)) register_4 (
    .D(demultiplexer_2_out3), .en(demultiplexer_1_out3), .Q(register_4_q), .clk(\Saat_Girişi ));  // open: clr
  Register #(.width(12)) register_5 (
    .D(demultiplexer_2_out4), .en(demultiplexer_1_out4), .Q(register_5_q), .clk(\Saat_Girişi ));  // open: clr
  Register #(.width(12)) register_6 (
    .D(demultiplexer_2_out5), .en(demultiplexer_1_out5), .Q(register_6_q), .clk(\Saat_Girişi ));  // open: clr
  Register #(.width(12)) register_7 (
    .D(demultiplexer_2_out6), .en(demultiplexer_1_out6), .Q(register_7_q), .clk(\Saat_Girişi ));  // open: clr
  Register #(.width(12)) register_8 (
    .D(demultiplexer_2_out7), .en(demultiplexer_1_out7), .Q(register_8_q), .clk(\Saat_Girişi ));  // open: clr
  Multiplexer #(.select(3), .width(12)) multiplexer_1 (
    .in0(register_1_q), .in1(register_2_q), .in2(register_3_q), .in3(register_4_q), .in4(register_5_q),
    .in5(register_6_q), .in6(register_7_q), .in7(register_8_q), .out(\KY1_Veri_Çıkış ),
    .sel(\KY1_Adres_Giriş ));  // open: en
  Multiplexer #(.select(3), .width(12)) multiplexer_2 (
    .in0(register_1_q), .in1(register_2_q), .in2(register_3_q), .in3(register_4_q), .in4(register_5_q),
    .in5(register_6_q), .in6(register_7_q), .in7(register_8_q), .out(\KY2_Veri_Çıkış ),
    .sel(\KY2_Adres_Giriş ));  // open: en
endmodule
